// Digital circuit c61.dig as structural Verilog
module c61 (
  input  in_1
);

  wire and_1_out, and_2_out, and_3_out, and_4_out, and_5_out, and_6_out, and_9_out, and_10_out, and_11_out,
       and_12_out, and_13_out, comparator_1_eq, comparator_2_eq, delay_1_out, delay_2_out, delay_3_out,
       isjmp_s1_nq, mrsel_s2_q, nand_1_out, not_1_out, not_2_out, or_1_out, or_2_out, or_4_out, RST_out,
       valid_s1_nq, valid_s1_q, wbe_0_q, wbe_1_q, xor_1_out;
  wire [1:0] and_7_out, multiplexer_5_out, or_3_out;
  wire [1:1] and_8_out, ext_s1_q;
  wire [2:0] dst_s2_q, INSN_q, insn_s1_q, multiplexer_1_out, multiplexer_4_out, multiplexer_6_out, RA_q, RB_q;
  wire [3:0] dst_s1_q;
  wire [3:3] RASET_q;
  wire [5:0] add_1_s, add_2_s, add_4_s, IMM_q, membase_q, multiplexer_2_out, multiplexer_3_out,
       multiplexer_7_out, multiplexer_8_out, multiplexer_9_out, multiplexer_10_out, multiplexer_11_out,
       multiplexer_12_out, multiplexer_13_out, neg_1_out, out_s2_q, ramdualport_1_d, rasrc_s1_q, raval_s1_q,
       rbim_s1_q, REGS_0_da, REGS_0_db, REGS_1_da, REGS_1_db, xor_2_out;
  wire [9:0] add_3_s;
  wire [15:0] INSTR_ROM_d;

  not not_1 (not_1_out, in_1);
  Reset #(.invertOutput("false")) RST (.out(RST_out));
  ROM #(.AddrBits(6), .Bits(16)) INSTR_ROM (.A(REGS_0_da), .sel(1'b1), .D(INSTR_ROM_d));
  not not_2 (not_2_out, not_1_out);
  D_FF #(.Bits(3)) INSN (.D(INSTR_ROM_d[15:13]), .C(in_1), .Q(INSN_q));  // open: nQ
  D_FF #(.Bits(3)) RA (.D(INSTR_ROM_d[11:9]), .C(in_1), .Q(RA_q));  // open: nQ
  D_FF RASET (.D(INSTR_ROM_d[12]), .C(in_1), .Q(RASET_q[3]));  // open: nQ
  D_FF #(.Bits(3)) RB (.D(INSTR_ROM_d[8:6]), .C(in_1), .Q(RB_q));  // open: nQ
  D_FF #(.Bits(6)) IMM (.D(INSTR_ROM_d[5:0]), .C(in_1), .Q(IMM_q));  // open: nQ
  xor xor_1 (xor_1_out, in_1, not_2_out);
  Delay #(.delayTime(2)) delay_1 (.in(in_1), .out(delay_1_out));
  Multiplexer #(.Bits(3)) multiplexer_1 (.sel(delay_1_out), .in_0(3'b111), .in_1(RA_q), .out(multiplexer_1_out));
  and and_1 (and_1_out, INSN_q[0], INSN_q[1], INSN_q[2]);
  Delay #(.delayTime(2)) delay_2 (.in(in_1), .out(delay_2_out));
  Multiplexer #(.Bits(6)) multiplexer_2 (.sel(RST_out), .in_0(add_1_s), .in_1({6{1'b0}}), .out(multiplexer_2_out));
  Multiplexer #(.Bits(6)) multiplexer_3 (
    .sel(delay_2_out), .in_0(multiplexer_2_out), .in_1(multiplexer_13_out), .out(multiplexer_3_out));
  Delay #(.delayTime(2)) delay_3 (.in(in_1), .out(delay_3_out));
  Multiplexer #(.Bits(3)) multiplexer_4 (.sel(and_1_out), .in_0(3'b000), .in_1(RB_q), .out(multiplexer_4_out));
  RegisterFile #(.AddrBits(3), .Bits(6)) REGS_0 (
    .Din(multiplexer_3_out), .we(or_1_out), .Rw(multiplexer_6_out), .C(xor_1_out), .Ra(multiplexer_1_out),
    .Rb(RB_q), .Da(REGS_0_da), .Db(REGS_0_db));
  RegisterFile #(.AddrBits(3), .Bits(6)) REGS_1 (
    .Din(multiplexer_13_out), .we(and_13_out), .Rw(dst_s2_q), .C(xor_1_out), .Ra(RA_q),
    .Rb(multiplexer_4_out), .Da(REGS_1_da), .Db(REGS_1_db));
  Multiplexer #(.Bits(2)) multiplexer_5 (.sel(and_1_out), .in_0(2'b01), .in_1(IMM_q[1:0]), .out(multiplexer_5_out));
  Multiplexer #(.Bits(3)) multiplexer_6 (.sel(delay_3_out), .in_0(3'b111), .in_1(dst_s2_q), .out(multiplexer_6_out));
  or or_1 (or_1_out, ~delay_3_out, and_12_out);  // Or
  Add #(.Bits(6)) add_1 (.a(REGS_0_da), .b(6'b000001), .c_i(1'b0), .s(add_1_s));  // open: c_o
  Multiplexer #(.Bits(6)) multiplexer_7 (.sel(RASET_q[3]), .in_0(REGS_0_da), .in_1(REGS_1_da), .out(multiplexer_7_out));
  Comparator #(.Bits(4)) comparator_1 (.a({RASET_q[3], RA_q}), .b(4'b0111), .eq(comparator_1_eq));  // open: gt, lt
  Add #(.Bits(6)) add_2 (.a(REGS_0_db), .b(IMM_q), .c_i(1'b0), .s(add_2_s));  // open: c_o
  Multiplexer #(.Bits(6)) multiplexer_8 (.sel(and_1_out), .in_0(add_2_s), .in_1(IMM_q), .out(multiplexer_8_out));
  Multiplexer #(.Selector_Bits(2), .Bits(6)) multiplexer_9 (
    .sel(multiplexer_5_out), .in_0(multiplexer_7_out), .in_1(add_1_s), .in_2(REGS_1_db),
    .in_3({multiplexer_7_out[4:0], 1'b0}), .out(multiplexer_9_out));
  D_FF valid_s1 (.D(or_2_out), .C(not_1_out), .Q(valid_s1_q), .nQ(valid_s1_nq));
  D_FF #(.Bits(4)) dst_s1 (.D({RASET_q[3], RA_q}), .C(not_1_out), .Q(dst_s1_q));  // open: nQ
  D_FF isjmp_s1 (.D(comparator_1_eq), .C(not_1_out), .nQ(isjmp_s1_nq));  // open: Q
  D_FF #(.Bits(6)) rbim_s1 (.D(multiplexer_8_out), .C(not_1_out), .Q(rbim_s1_q));  // open: nQ
  D_FF #(.Bits(6)) rasrc_s1 (.D(multiplexer_9_out), .C(not_1_out), .Q(rasrc_s1_q));  // open: nQ
  D_FF #(.Bits(6)) membase (.D(REGS_1_db), .C(not_1_out), .Q(membase_q));  // open: nQ
  D_FF #(.Bits(6)) raval_s1 (.D(multiplexer_7_out), .C(not_1_out), .Q(raval_s1_q));  // open: nQ
  D_FF #(.Bits(3)) insn_s1 (.D(INSN_q), .C(not_1_out), .Q(insn_s1_q));  // open: nQ
  D_FF ext_s1 (.D(and_1_out), .C(not_1_out), .Q(ext_s1_q[1]));  // open: nQ
  D_FF extmode_s1 (.D(IMM_q[5]), .C(not_1_out));  // open: Q, nQ
  D_FF extsel_s1 (.D(IMM_q[4]), .C(not_1_out));  // open: Q, nQ
  D_FF #(.Bits(2)) extop_s1 (.D(IMM_q[3:2]), .C(not_1_out));  // open: Q, nQ
  or or_2 (or_2_out, valid_s1_nq, and_11_out);
  and and_2 (and_2_out, valid_s1_q, nand_1_out);
  Neg #(.Bits(6)) neg_1 (.in(rbim_s1_q), .out(neg_1_out));
  Multiplexer #(.Bits(6)) multiplexer_10 (
    .sel(insn_s1_q[0]), .in_0(rbim_s1_q), .in_1(raval_s1_q), .out(multiplexer_10_out));
  and and_3 (and_3_out, insn_s1_q[2], ~insn_s1_q[1], add_3_s[9]);  // And
  Add #(.Bits(10)) add_3 (
    .a({4'b0000, multiplexer_10_out}), .b({membase_q, 4'b0000}), .c_i(1'b0), .s(add_3_s));  // open: c_o
  and and_4 (and_4_out, and_2_out, ~dst_s1_q[3]);  // And
  and and_5 (and_5_out, dst_s1_q[3], and_2_out);
  Multiplexer #(.Bits(6)) multiplexer_11 (
    .sel(and_6_out), .in_0(rbim_s1_q), .in_1(neg_1_out), .out(multiplexer_11_out));
  and and_6 (and_6_out, ~insn_s1_q[0], insn_s1_q[1]);  // And
  and and_7 (and_7_out[1], insn_s1_q[0], insn_s1_q[1], ~insn_s1_q[2]);  // And
  nor nor_1 (and_7_out[0], insn_s1_q[0], insn_s1_q[1], insn_s1_q[2]);
  and and_8 (and_8_out[1], ~add_3_s[9], ~insn_s1_q[1], insn_s1_q[2]);  // And
  Add #(.Bits(6)) add_4 (.a(multiplexer_11_out), .b(raval_s1_q), .c_i(1'b0), .s(add_4_s));  // open: c_o
  assign xor_2_out = rbim_s1_q ^ raval_s1_q;  // XOr xor_2, 6 bits wide
  nand nand_1 (nand_1_out, and_6_out, ~insn_s1_q[2]);  // NAnd
  Multiplexer #(.Selector_Bits(2), .Bits(6)) multiplexer_12 (
    .sel(or_3_out), .in_0(add_4_s), .in_1(rbim_s1_q), .in_2(xor_2_out), .in_3(rasrc_s1_q),
    .out(multiplexer_12_out));
  assign or_3_out = and_7_out | {2{and_8_out[1]}} | {2{ext_s1_q[1]}};  // Or or_3, 2 bits wide
  and and_9 (and_9_out, insn_s1_q[0], and_8_out[1]);
  and and_10 (and_10_out, and_8_out[1], ~insn_s1_q[0]);  // And
  and and_11 (and_11_out, isjmp_s1_nq, or_4_out);
  Comparator #(.Signed("true"), .Bits(6)) comparator_2 (
    .a(multiplexer_12_out), .b({6{1'b0}}), .eq(comparator_2_eq));  // open: gt, lt
  or or_4 (or_4_out, comparator_2_eq, nand_1_out);
  D_FF mrsel_s2 (.D(and_10_out), .C(delay_3_out), .Q(mrsel_s2_q));  // open: nQ
  D_FF wbe_0 (.D(and_4_out), .C(delay_3_out), .Q(wbe_0_q));  // open: nQ
  D_FF #(.Bits(3)) dst_s2 (.D(dst_s1_q[2:0]), .C(delay_3_out), .Q(dst_s2_q));  // open: nQ
  D_FF wbe_1 (.D(and_5_out), .C(delay_3_out), .Q(wbe_1_q));  // open: nQ
  D_FF #(.Bits(6)) out_s2 (.D(multiplexer_12_out), .C(delay_3_out), .Q(out_s2_q));  // open: nQ
  RAMDualPort #(.AddrBits(9), .Bits(6)) ramdualport_1 (
    .A(add_3_s[8:0]), .Din(rbim_s1_q), .str(and_9_out), .C(delay_3_out), .ld(and_10_out), .D(ramdualport_1_d));
  and and_12 (and_12_out, wbe_0_q, delay_3_out);
  and and_13 (and_13_out, wbe_1_q, delay_3_out);
  Multiplexer #(.Bits(6)) multiplexer_13 (
    .sel(mrsel_s2_q), .in_0(out_s2_q), .in_1(ramdualport_1_d), .out(multiplexer_13_out));

  // Notes on the sheet:
  //   contents of INSTR_ROM (hex, n*v repeats v):
  //   10,248,2001,4040,4bf,44c0,f84,628b,6000,12d1,0,a040,d381,2200,53bf,f91,cf86,1181,
  //   8980,8b81,0,2940
  //   CLK_TRANS
  //   WBE_B2
  //   RA_COMB
  //   RESULT
  //   OP_EXT
  //   ADDR_NEXT
  //   ADDR_INS
  //   WSEL_B1
  //   SRC_SEL
  //   WBE_B1
  //   RB+IMM
  //   IMM
  //   .RA
  //   .RA_B0+1
  //   .RB_B2
  //   .RA<<1
  //   OP_IO
  //   WBE
  //   A_DATA
  //   ~MEM/IO
  //   OP_SUBCMP
  //   F_ZERO
  //   OP_XOR
  //   OP_MOV
  //   OP_MEM
  //   ~WRITEBACK
  //   ~OP_IFEQ
  //   ~SKIPNEXT
  //   RES_ALU
  //   OP_STORE
  //   OP_LOAD
endmodule
